# Fritzing sketch SenseoWifi-PCB (saved by Fritzing 0.9.3b)
circuit board: 3.30498cm x 7.22197cm
breadboards: 1

parts:
  U1 = PC817
  PC847X_/_4×PC817X = PC817
  U2 = PC817
  R5 = Resistor [tolerance=±5% resistance=150 package=THT]
  R4 = Resistor [tolerance=±5% resistance=1k package=THT]
  R1 = Resistor [tolerance=±5% resistance=470 package=THT]
  R3 = Resistor [tolerance=±5% resistance=470 package=THT]
  U3 = PC817
  T1_____T2_____TP = male pin header, 3 pins [form="♂ (male)"]
  GND = male pin header, 1 pin [form="♂ (male)"]
  LED = male pin header, 1 pin [form="♂ (male)"]
  R2 = Resistor [tolerance=±5% resistance=470 package=THT]
  Buzzer = Buzzer 12mm [package=buzzer-12mm-ns-kit]
  J1 = male pin header, 8 pins [form="♂ (male)"]
  J2 = male pin header, 7 pins [form="♂ (male)"]
  WeMos_D1_Mini = WeMos D1 Mini
  TCRT5000(AD-+) = male pin header, 4 pins [form="♂ (male)"]

nets:
  N1: U1.connector0, R2.Pin_1
  GND: U1.connector1, PC847X_/_4×PC817X.connector1, U2.connector5, U3.connector1, Buzzer.2, J2.pin1, WeMos_D1_Mini.G, TCRT5000(AD-+).pin2
  N2: U1.connector3, T1_____T2_____TP.pin2
  N3: U1.connector5, PC847X_/_4×PC817X.connector5, U2.connector1, U3.connector5, GND.pin1
  N4: PC847X_/_4×PC817X.connector0, R1.Pin_1
  N5: PC847X_/_4×PC817X.connector3, T1_____T2_____TP.pin1
  N6: U2.connector0, R4.Pin_1
  N7: U2.connector3, J1.pin3, WeMos_D1_Mini.D7
  N8: R5.Pin_0, J1.pin2, WeMos_D1_Mini.D8
  N9: R5.Pin_1, Buzzer.1
  N10: R4.Pin_0, LED.pin1
  N11: R1.Pin_0, J1.pin5, WeMos_D1_Mini.D5
  N12: R3.Pin_0, J2.pin5, WeMos_D1_Mini.D1
  N13: R3.Pin_1, U3.connector0
  N14: U3.connector3, T1_____T2_____TP.pin3
  N15: R2.Pin_0, J2.pin4, WeMos_D1_Mini.D2
  N16: J1.pin1, WeMos_D1_Mini.3V3
  N17: J1.pin4, WeMos_D1_Mini.D6, TCRT5000(AD-+).pin3
  N18: J1.pin6, WeMos_D1_Mini.D0
  N19: J1.pin7, WeMos_D1_Mini.A0, TCRT5000(AD-+).pin4
  N20: J1.pin8, WeMos_D1_Mini.RST
  N21: J2.pin2, WeMos_D1_Mini.D4
  N22: J2.pin3, WeMos_D1_Mini.D3
  N23: J2.pin6, WeMos_D1_Mini.RX
  N24: J2.pin7, WeMos_D1_Mini.TX
  N25: WeMos_D1_Mini.5V, TCRT5000(AD-+).pin1

notes:
  -->
  SenseoWifi - PCB v1.0
  http://github.com/ThomDietrich/SenseoWifi
  Senseo Connections
